# Fritzing sketch ArduinoAQI (saved by Fritzing 0.9.3b)

parts:
  WeMos_D1_R1 = WeMos D1 R2
  Grove1 = Grove 4 Digit Display
  WiFi_Reset = Pushbutton [package="[THT]"]

nets:
  N1: WeMos_D1_R1.D11, WiFi_Reset.Pin_3
  N2: WeMos_D1_R1.D12, Grove1.DIO
  N3: WeMos_D1_R1.D13, Grove1.CLK
  N4: WeMos_D1_R1.GND#15, WiFi_Reset.Pin_1
  N5: WeMos_D1_R1.GND#21, Grove1.GND
  5V: WeMos_D1_R1.5V, Grove1.VCC

custom parts:
  WeMos D1 R2: The D1 R2 is a mini wifi board based on the ESP-8266EX.
